# Fritzing sketch ElectricalSketch (saved by Fritzing 0.9.3b)
breadboards: 1

parts:
  Part1 = Arduino Mega 2560 (Rev3)
  BAT1 = Battery Holders [package=lipo-1100mAh]
  Pololu_A1 = Pololu A4988 [package=SO16]
  Pololu_A2 = Pololu A4988 [package=SO16]
  Pololu_A3 = Pololu A4988 [package=SO16]
  M1 = Stepper Motor - Bipolar
  M2 = Stepper Motor - Bipolar
  M3 = Stepper Motor - Bipolar
  C1 = Ceramic Capacitor [capacitance=100nF package="100 mil [THT, multilayer]"]
  C2 = Ceramic Capacitor [capacitance=100nF package="100 mil [THT, multilayer]"]
  C3 = Ceramic Capacitor [capacitance="100 nF" package="0603 [SMD, multilayer]"]

nets:
  GND: Part1.GND, BAT1.-, Pololu_A1.GND, Pololu_A2.GND#14, Pololu_A3.GND#14, C1.1, C2.1, C3.1
  VIN: Part1.VIN, Pololu_A1.VDD
  N1: Part1.D2_PWM, Pololu_A3.DIR
  N2: Part1.D3_PWM, Pololu_A3.STEP
  N3: Part1.D4_PWM, Pololu_A2.DIR
  N4: Part1.D5_PWM, Pololu_A2.STEP
  N5: Part1.D6_PWM, Pololu_A1.DIR
  N6: Part1.D7_PWM, Pololu_A1.STEP
  N7: BAT1.+, Pololu_A1.VMOT, Pololu_A2.VMOT, Pololu_A3.VMOT, C1.0, C2.0, C3.0
  N8: Pololu_A1.RESET, Pololu_A1.SLEEP
  N9: Pololu_A1.1B, M1.D
  N10: Pololu_A1.1A, M1.B
  N11: Pololu_A1.2A, M1.C
  N12: Pololu_A1.2B, M1.A
  N13: Pololu_A2.RESET, Pololu_A2.SLEEP
  N14: Pololu_A2.1B, M3.D
  N15: Pololu_A2.1A, M3.B
  N16: Pololu_A2.2A, M3.C
  N17: Pololu_A2.2B, M3.A
  N18: Pololu_A3.RESET, Pololu_A3.SLEEP
  N19: Pololu_A3.1B, M2.D
  N20: Pololu_A3.1A, M2.B
  N21: Pololu_A3.2A, M2.C
  N22: Pololu_A3.2B, M2.A

notes:
  11.1V 3S Lipo Battery
